# Fritzing sketch circuit (saved by Fritzing 0.9.4)
breadboards: 1

parts:
  Bauteil1 = Adafruit TPL5110 Power Timer [part_number="Adafruit #3435"]
  Raspberry_Pi_1 = Raspberry Pi 3 [part_number=RPI-3-V1.2]
  Bauteil2 = Adafruit Micro USB Breakout [part_number="Adafruit #1833"]
  R1 = Resistor [tolerance=±5% resistance=180k package="0805 [SMD]"]
  R2 = Resistor [tolerance=±5% resistance=100k package="0805 [SMD]"]
  R3 = Resistor [tolerance=±5% resistance=10k package="0805 [SMD]"]
  C1 = Capacitor Polarized [package=cpol-radial-100uf-25v]

nets:
  N1: Bauteil1.VDD, Bauteil2.VBUS
  GND: Bauteil1.GND, Raspberry_Pi_1.GND, Bauteil2.GND, R1.Pin_0, R2.Pin_0, C1.-
  N2: Bauteil1.DELAY, R1.Pin_1
  N3: Bauteil1.PWROUT, Raspberry_Pi_1.5V
  N4: Bauteil1.DONE, R2.Pin_1, R3.Pin_1, C1.+
  N5: Raspberry_Pi_1.GPIO12, R3.Pin_0

custom parts:
  Adafruit TPL5110 Power Timer: With some development boards, low power usage is an afterthought. Especially when price and usability is the main selling point. So what should you do when its time to turn around and make that project of yours run on a battery or solar? Sure you could try to hot-air that regulator off, or you could jerry-rig a relay. Or, use a 555? Ugh, the options aren't that great. The Adafruit TPL5110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
  Adafruit Micro USB Breakout: Simple but effective - this breakout board has a USB Micro-B connector, with all 5 pins broken out. Great for pairing with a microcontroller with USB support, or adding USB 5V power to a project. We use a micro-AB connector with through-hole shielding pads for an excellent strong connection - it won't rip off by accident! Comes with one fully assembled and tested micro B breakout PCB and a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
